# Fritzing sketch Untitled Sketch 4 (saved by Fritzing 0.9.2b)
breadboards: 2

parts:
  R1 = Resistor [tolerance=±5% resistance=220 package=THT]
  LED2 = smd LED [color="Red (633nm)" package="0805 [SMD]"]
  LED3 = smd LED [color="Red (633nm)" package="0805 [SMD]"]
  U2 = TLP621 [package=THT]
  U3 = TLP621 [package=THT]
  R2 = Resistor [tolerance=±5% resistance=220 package=THT]
  R3 = Resistor [tolerance=±5% resistance=220 package=THT]
  R4 = Resistor [tolerance=±5% resistance=220 package=THT]
  Q2 = NPN-Transistor [package="TO92 [THT]"]
  D2 = Rectifier Diode [part_number=1N4007 package="300 mil [THT]"]
  D3 = Rectifier Diode [part_number=1N4007 package="300 mil [THT]"]
  U4 = RELAY [package=relay-jzc]
  U5 = RELAY [package=relay-jzc]
  JP2 = Header 3 [package=screwterminal-3.5mm-3_lock.007s]
  JP3 = Header 3 [package=screwterminal-3.5mm-3_lock.007s]
  Part1 = Arduino Nano (Rev3.0)
  Q3 = NPN-Transistor [package="TO92 [THT]"]

nets:
  N1: R1.Pin_0, U2.Pin_4, U3.Pin_4, R2.Pin_1, Q2.C, D2.anode, D3.anode, Part1.VIN, Q3.C
  N2: R1.Pin_1, U2.Pin_1
  N3: LED2.cathode, Part1.D6
  N4: LED2.anode, U2.Pin_2
  N5: LED3.cathode, Part1.D7
  N6: LED3.anode, U3.Pin_2
  N7: U2.Pin_3, R4.Pin_0
  N8: U3.Pin_1, R2.Pin_0
  N9: U3.Pin_3, R3.Pin_1
  N10: R3.Pin_0, Q2.B
  N11: R4.Pin_1, Q3.B
  N12: Q2.E, Part1.GND, Q3.E
  N13: U4.NC, JP2.1
  N14: U4.NO, JP2.3
  N15: U4.MAIN, JP2.2
  N16: U5.NC, JP3.1
  N17: U5.NO, JP3.3
  N18: U5.MAIN, JP3.2
